# Fritzing sketch line following robot with ardumoto IR sensor(1) (saved by Fritzing 0.9.3b)
circuit board: 8.48074cm x 3.78819cm
breadboards: 1

parts:
  LED8 = LED - 5mm [color="Blue (430nm)" package="5 mm [THT]"]
  LED9 = LED - 5mm [color="Blue (430nm)" package="5 mm [THT]"]
  LED10 = LED - 5mm [color="Blue (430nm)" package="5 mm [THT]"]
  LED11 = LED - 3mm [color="Infrared (880nm)" package="3 mm [THT]"]
  PTD = LED - 3mm [color="Infrared (880nm)" package="3 mm [THT]"]
  R7 = Resistor [tolerance=±5% resistance=220 package=THT]
  R8 = Resistor [tolerance=±5% resistance=220 package=THT]
  R9 = Resistor [tolerance=±5% resistance=220 package=THT]
  R10 = Resistor [tolerance=±5% resistance=10k package=THT]
  R11 = Resistor [tolerance=±5% resistance=10k package=THT]
  R12 = Resistor [tolerance=±5% resistance=10k package=THT]
  J2 = female pin header, 5 pins [form="♀ (female)"]
  LED12 = LED - 3mm [color="Infrared (880nm)" package="3 mm [THT]"]

nets:
  N1: LED8.cathode, LED9.cathode, LED10.cathode, LED11.anode, PTD.anode, J2.pin1, LED12.anode
  N2: LED8.anode, R8.Pin_0
  N3: LED9.anode, R7.Pin_0
  N4: LED10.anode, R9.Pin_0
  N5: LED11.cathode, R11.Pin_0, J2.pin3
  N6: PTD.cathode, R10.Pin_0, J2.pin2
  N7: R7.Pin_1, R8.Pin_1, R9.Pin_1, J2.pin5
  N8: R10.Pin_1, R11.Pin_1, R12.Pin_1
  N9: R12.Pin_0, J2.pin4, LED12.cathode

notes:
  5 V
  A0
  GND
  A1
  A2
