# Fritzing sketch bluetooth PCB (saved by Fritzing 0.9.3b)
circuit board: 7.12259cm x 5.37562cm
breadboards: 1

parts:
  J1 = female pin header, 9 pins [form="♀ (female)"]
  R1 = TRIMPOT [package=3386u]
  LED1 = LED - 5mm [color="Red (633nm)" package="5 mm [THT]"]
  Part1 = Arduino Uno (Rev3)
  R2 = Resistor [tolerance=±5% resistance=220 package="2010 [SMD]"]

nets:
  5V: J1.pin1, R1.CCW, Part1.5V, R2.Pin_0
  GND: J1.pin2, R1.CW, LED1.cathode, LED1.anode, Part1.GND, R2.Pin_1
  N1: J1.pin3, Part1.D4
  N2: J1.pin5, Part1.D7
  N3: J1.pin6, Part1.D8
  N4: J1.pin7, Part1.D11_PWM/MOSI
  N5: J1.pin8, Part1.D12/MISO
  N6: J1.pin9, Part1.D13/SCK
  N7: R1.WIPER, Part1.A0

notes:
  power and ground lines for servo motor-> make it thick!
